# Fritzing sketch wiring-diagram (saved by Fritzing 0.9.6b)
breadboards: 1

parts:
  MCU1 = Raspberry Pi Zero
  LCD1 = LCD screen
  S2 = Pushbutton [package="[SMD]"]
  R1 = Resistor [tolerance=±5% resistance=1k power=0.25 package=THT]
  U3 = POT [package=trim_pot]
  8_Channel_Relay1 = 8 Channel Power Relay
  R4 = Resistor [tolerance=±5% resistance=1k power=0.25 package=THT]
  LED1 = LEDs [package=led10mm]

nets:
  VDD: MCU1.pin_2, MCU1.pin_4, LCD1.VDD, 8_Channel_Relay1.VCC
  N1: MCU1.pin_5, S2.Pin_3, S2.Pin_4, R1.Pin_0
  VSS: MCU1.pin_6, MCU1.pin_9, MCU1.pin_34, MCU1.pin_39, LCD1.VSS, LCD1.R/W, LCD1.LED-, S2.Pin_1, S2.Pin_2, R1.Pin_1, U3.S, 8_Channel_Relay1.GND, LED1.C
  N2: MCU1.pin_18, R4.Pin_1
  N3: MCU1.pin_22, 8_Channel_Relay1.IN1
  N4: MCU1.pin_23, LCD1.LED+
  N5: MCU1.pin_24, 8_Channel_Relay1.IN2
  N6: MCU1.pin_26, 8_Channel_Relay1.IN3
  N7: MCU1.pin_27, LCD1.DB7
  N8: MCU1.pin_28, 8_Channel_Relay1.IN4
  N9: MCU1.pin_29, LCD1.DB6
  N10: MCU1.pin_31, LCD1.DB5
  N11: MCU1.pin_33, LCD1.DB4
  N12: MCU1.pin_35, LCD1.E
  N13: MCU1.pin_37, LCD1.RS
  N14: LCD1.V0, U3.E

custom parts:
  8 Channel Power Relay: An 8 channel power relay. The module operates at 5V.
